// Logisim project processor.circ as structural Verilog: 23 circuits, main circuit MUX_2X1
module main (
  input  reset,
  output [7:0] out_2
);

  wire alu_1_z, and_1_out, BranchZero, clock_1_out, FlagWrite, IR_Load, Jump, MemWrite, or_1_out, PC_Enable,
       PC_Jump_Taken, ReadA_Sel, RegWrite, WriteRegSel, Z_value;
  wire [1:0] ALUSel, mux_2x1_1_out_4, mux_2x1_2_out_4, WriteBackSel;
  wire [2:0] control_unit_1_controlword;
  wire [3:0] alu_1_op, IMM, instruction_register_1_opcode, mux_4_bit_4x1_1_y, ram_1_dout,
       register_file_1_readdata_a, register_file_1_readdata_b;
  wire [7:0] instruction_memory_1_ins_reg, Jump_Addr;

  Clock clock_1 (.out(clock_1_out));
  or or_1 (or_1_out, PC_Enable, PC_Jump_Taken);
  // Probe on MemWrite
  RAM #(.addrWidth(4), .dataWidth(4)) ram_1 (
    .addr(IMM), .we(MemWrite), .oe(1'b1), .clk(clock_1_out), .din(register_file_1_readdata_a),
    .dout(ram_1_dout));
  Program_Counter program_counter_1 (
    .PC_enable(or_1_out), .CLock(clock_1_out), .PC_Jump_Taken(PC_Jump_Taken), .Reset(reset),
    .JUMP_Addr(Jump_Addr), .OP(out_2));
  Register_File register_file_1 (
    .WriteReg(mux_2x1_2_out_4), .ReadReg_A(mux_2x1_1_out_4), .WriteData(mux_4_bit_4x1_1_y),
    .RegWrite(RegWrite), .clock(clock_1_out), .ReadReg_B(IMM[1:0]), .ReadData_A(register_file_1_readdata_a),
    .ReadData_B(register_file_1_readdata_b));
  MUX_2X1 mux_2x1_1 (.S(ReadA_Sel), .A(IMM[3:2]), .B(2'b00), .out_4(mux_2x1_1_out_4));
  Register #(.width(1)) Flag_zero (.D(alu_1_z), .en(FlagWrite), .clk(clock_1_out), .Q(Z_value), .clr(reset));
  Instruction_Memory instruction_memory_1 (
    .PC(out_2), .IR_Enable(IR_Load), .Clock(clock_1_out), .Reset(reset),
    .INS_REG(instruction_memory_1_ins_reg));  // open: Operand, Reg_B, Reg_A, OPCODE
  ALU alu_1 (
    .ALU_Sel(ALUSel), .A(register_file_1_readdata_a), .B(register_file_1_readdata_b), .OP(alu_1_op),
    .Z(alu_1_z));
  // Probe on instruction_memory_1_ins_reg
  MUX_2X1 mux_2x1_2 (.S(WriteRegSel), .A(IMM[3:2]), .B(2'b00), .out_4(mux_2x1_2_out_4));
  // Probe on instruction_register_1_opcode
  // Probe on IMM
  Instruction_Register instruction_register_1 (
    .Instruction_In(instruction_memory_1_ins_reg), .IR_Load(IR_Load), .Clock(clock_1_out), .Operand(IMM),
    .Opcode(instruction_register_1_opcode));
  MUX_4_Bit_4X1 mux_4_bit_4x1_1 (
    .I0(alu_1_op), .I1(ram_1_dout), .S0(WriteBackSel[0]), .S1(WriteBackSel[1]), .I2(IMM), .I3(4'b0000),
    .Y(mux_4_bit_4x1_1_y));
  and and_1 (and_1_out, BranchZero, Z_value);
  // Probe on {PC_Enable, IR_Load, RegWrite, MemWrite, WriteBackSel, WriteRegSel, ALUSel, FlagWrite, Jump, BranchZero, ReadA_Sel, control_unit_1_controlword}
  Control_Unit control_unit_1 (
    .CLK(clock_1_out), .Reset(reset), .Opcode(instruction_register_1_opcode),
    .ControlWord({PC_Enable, IR_Load, RegWrite, MemWrite, WriteBackSel, WriteRegSel, ALUSel, FlagWrite, Jump, BranchZero, ReadA_Sel, control_unit_1_controlword}));  // open: out_5, out_6
  assign Jump_Addr = {{4{1'b0}}, IMM};  // Bit_Extender bit_extender_1
  or or_2 (PC_Jump_Taken, and_1_out, Jump);

  // Other names for the same wires on the sheet: Reg_B[1:0] = IMM[1:0]; Reg_A[1:0] = IMM[3:2]
endmodule

module MUX_2X1 (
  input  S,
  input  [1:0] A,
  input  [1:0] B,
  output [1:0] out_4
);

  wire and_1_out, and_2_out, and_3_out, and_4_out, not_1_out, not_2_out;

  not not_1 (not_1_out, S);
  not not_2 (not_2_out, S);
  and and_1 (and_1_out, A[0], not_1_out);
  and and_2 (and_2_out, S, B[0]);
  and and_3 (and_3_out, A[1], not_2_out);
  and and_4 (and_4_out, S, B[1]);
  or or_1 (out_4[0], and_1_out, and_2_out);
  or or_2 (out_4[1], and_3_out, and_4_out);
endmodule

module MUX_4_Bit (
  input  [3:0] A,
  input  [3:0] B,
  input  S,
  output [3:0] out_4
);

  wire and_1_out, and_2_out, and_3_out, and_4_out, and_5_out, and_6_out, and_7_out, and_8_out, not_1_out,
       not_2_out, not_3_out, not_4_out;

  not not_1 (not_1_out, S);
  not not_2 (not_2_out, S);
  not not_3 (not_3_out, S);
  not not_4 (not_4_out, S);
  and and_1 (and_1_out, A[0], not_1_out);
  and and_2 (and_2_out, S, B[0]);
  and and_3 (and_3_out, A[1], not_2_out);
  and and_4 (and_4_out, S, B[1]);
  and and_5 (and_5_out, A[2], not_3_out);
  and and_6 (and_6_out, S, B[2]);
  and and_7 (and_7_out, A[3], not_4_out);
  and and_8 (and_8_out, S, B[3]);
  or or_1 (out_4[0], and_1_out, and_2_out);
  or or_2 (out_4[1], and_3_out, and_4_out);
  or or_3 (out_4[2], and_5_out, and_6_out);
  or or_4 (out_4[3], and_7_out, and_8_out);
endmodule

module Decoder_2_4 (
  input  [1:0] in_1,
  output Y0,
  output Y1,
  output Y2,
  output Y3
);

  wire not_1_out, not_2_out;

  not not_1 (not_1_out, in_1[1]);
  not not_2 (not_2_out, in_1[0]);
  and and_1 (Y0, not_1_out, not_2_out);
  and and_2 (Y1, not_1_out, in_1[0]);
  and and_3 (Y2, in_1[1], not_2_out);
  and and_4 (Y3, in_1[1], in_1[0]);
endmodule

module Adder_1_Bit (
  input  A,
  input  B,
  input  C_in,
  output Sum,
  output C_out
);

  wire and_1_out, and_2_out, xor_1_out;

  xor xor_1 (xor_1_out, A, B);
  xor xor_2 (Sum, xor_1_out, C_in);
  and and_1 (and_1_out, A, B);
  and and_2 (and_2_out, xor_1_out, C_in);
  or or_1 (C_out, and_2_out, and_1_out);
endmodule

module Adder_4_Bit (
  input  [3:0] A,
  input  [3:0] B,
  output [3:0] OP,
  output Overflow
);

  wire adder_1_bit_1_c_out, adder_1_bit_2_c_out, adder_1_bit_3_c_out;

  Adder_1_Bit adder_1_bit_1 (.A(A[0]), .B(B[0]), .C_in(1'b0), .Sum(OP[0]), .C_out(adder_1_bit_1_c_out));
  Adder_1_Bit adder_1_bit_2 (.A(A[1]), .B(B[1]), .C_in(adder_1_bit_1_c_out), .Sum(OP[1]), .C_out(adder_1_bit_2_c_out));
  Adder_1_Bit adder_1_bit_3 (.A(A[2]), .B(B[2]), .C_in(adder_1_bit_2_c_out), .Sum(OP[2]), .C_out(adder_1_bit_3_c_out));
  Adder_1_Bit adder_1_bit_4 (.A(A[3]), .B(B[3]), .C_in(adder_1_bit_3_c_out), .Sum(OP[3]), .C_out(Overflow));
endmodule

module Complement_2s (
  input  [3:0] A,
  output [3:0] OP
);

  wire [3:0] not_1_out;

  assign not_1_out = ~A;  // NOT_Gate not_1, 4 bits wide
  Adder_4_Bit_carry_in adder_4_bit_carry_in_1 (.A(not_1_out), .C_in(1'b1), .B(4'b0000), .out_4(OP));  // open: Overflow
endmodule

module Adder_4_Bit_carry_in (
  input  [3:0] A,
  input  C_in,
  input  [3:0] B,
  output [3:0] out_4,
  output Overflow
);

  wire adder_1_bit_1_c_out, adder_1_bit_2_c_out, adder_1_bit_3_c_out;

  Adder_1_Bit adder_1_bit_1 (.A(A[0]), .B(B[0]), .C_in(C_in), .Sum(out_4[0]), .C_out(adder_1_bit_1_c_out));
  Adder_1_Bit adder_1_bit_2 (
    .A(A[1]), .B(B[1]), .C_in(adder_1_bit_1_c_out), .Sum(out_4[1]), .C_out(adder_1_bit_2_c_out));
  Adder_1_Bit adder_1_bit_3 (
    .A(A[2]), .B(B[2]), .C_in(adder_1_bit_2_c_out), .Sum(out_4[2]), .C_out(adder_1_bit_3_c_out));
  Adder_1_Bit adder_1_bit_4 (.A(A[3]), .B(B[3]), .C_in(adder_1_bit_3_c_out), .Sum(out_4[3]), .C_out(Overflow));
endmodule

module Subtract_4_Bit (
  input  [3:0] A,
  input  [3:0] B,
  output [3:0] OP,
  output Overflow
);

  wire [3:0] complement_2s_1_op;

  Complement_2s complement_2s_1 (.A(B), .OP(complement_2s_1_op));
  Adder_4_Bit adder_4_bit_1 (.A(A), .B(complement_2s_1_op), .OP(OP), .Overflow(Overflow));
endmodule

module AND_4_Bit (
  input  [3:0] A,
  input  [3:0] B,
  output [3:0] OP
);

  and and_1 (OP[0], A[0], B[0]);
  and and_2 (OP[1], A[1], B[1]);
  and and_3 (OP[2], A[2], B[2]);
  and and_4 (OP[3], A[3], B[3]);
endmodule

module DEC_1 (
  input  [3:0] A,
  output [3:0] OP
);

  Adder_4_Bit adder_4_bit_1 (.A(A), .B(4'b1111), .OP(OP));  // open: Overflow
endmodule

module ALU (
  input  [1:0] ALU_Sel,
  input  [3:0] A,
  input  [3:0] B,
  output [3:0] OP,
  output Z
);

  wire alu_supporter_1_out_3, alu_supporter_1_out_4, alu_supporter_1_out_5, alu_supporter_1_out_6,
       alu_supporter_2_out_3, alu_supporter_2_out_4, alu_supporter_2_out_5, alu_supporter_2_out_6,
       alu_supporter_3_out_3, alu_supporter_3_out_4, alu_supporter_3_out_5, alu_supporter_3_out_6,
       alu_supporter_4_out_3, alu_supporter_4_out_4, alu_supporter_4_out_5, alu_supporter_4_out_6,
       decoder_2_4_1_y0, decoder_2_4_1_y1, decoder_2_4_1_y2, decoder_2_4_1_y3, not_1_out, not_2_out,
       not_3_out, not_4_out;
  wire [3:0] adder_4_bit_1_op, and_4_bit_1_op, dec_1_1_op, subtract_4_bit_1_op;

  Adder_4_Bit adder_4_bit_1 (.A(A), .B(B), .OP(adder_4_bit_1_op));  // open: Overflow
  Subtract_4_Bit subtract_4_bit_1 (.A(A), .B(B), .OP(subtract_4_bit_1_op));  // open: Overflow
  AND_4_Bit and_4_bit_1 (.A(A), .B(B), .OP(and_4_bit_1_op));
  DEC_1 dec_1_1 (.A(A), .OP(dec_1_1_op));
  Decoder_2_4 decoder_2_4_1 (
    .in_1(ALU_Sel), .Y0(decoder_2_4_1_y0), .Y1(decoder_2_4_1_y1), .Y2(decoder_2_4_1_y2), .Y3(decoder_2_4_1_y3));
  ALU_Supporter alu_supporter_1 (
    .A(adder_4_bit_1_op), .an_d(decoder_2_4_1_y0), .out_3(alu_supporter_1_out_3),
    .out_4(alu_supporter_1_out_4), .out_5(alu_supporter_1_out_5), .out_6(alu_supporter_1_out_6));
  ALU_Supporter alu_supporter_2 (
    .A(subtract_4_bit_1_op), .an_d(decoder_2_4_1_y1), .out_3(alu_supporter_2_out_3),
    .out_4(alu_supporter_2_out_4), .out_5(alu_supporter_2_out_5), .out_6(alu_supporter_2_out_6));
  ALU_Supporter alu_supporter_3 (
    .A(and_4_bit_1_op), .an_d(decoder_2_4_1_y2), .out_3(alu_supporter_3_out_3),
    .out_4(alu_supporter_3_out_4), .out_5(alu_supporter_3_out_5), .out_6(alu_supporter_3_out_6));
  ALU_Supporter alu_supporter_4 (
    .A(dec_1_1_op), .an_d(decoder_2_4_1_y3), .out_3(alu_supporter_4_out_3), .out_4(alu_supporter_4_out_4),
    .out_5(alu_supporter_4_out_5), .out_6(alu_supporter_4_out_6));
  or or_1 (OP[0], alu_supporter_1_out_3, alu_supporter_2_out_3, alu_supporter_3_out_3, alu_supporter_4_out_3);
  or or_2 (OP[1], alu_supporter_1_out_4, alu_supporter_2_out_4, alu_supporter_3_out_4, alu_supporter_4_out_4);
  or or_3 (OP[2], alu_supporter_1_out_5, alu_supporter_2_out_5, alu_supporter_3_out_5, alu_supporter_4_out_5);
  or or_4 (OP[3], alu_supporter_1_out_6, alu_supporter_2_out_6, alu_supporter_3_out_6, alu_supporter_4_out_6);
  // Probe on OP[0]
  not not_1 (not_1_out, OP[1]);
  not not_2 (not_2_out, OP[0]);
  not not_3 (not_3_out, OP[2]);
  not not_4 (not_4_out, OP[3]);
  and and_1 (Z, not_1_out, not_2_out, not_3_out, not_4_out);
endmodule

module Register_File (
  input  [1:0] WriteReg,
  input  [1:0] ReadReg_A,
  input  [3:0] WriteData,
  input  RegWrite,
  input  clock,
  input  [1:0] ReadReg_B,
  output [3:0] ReadData_A,
  output [3:0] ReadData_B
);

  wire and_1_out, and_2_out, and_3_out, and_4_out, decoder_2_4_1_y0, decoder_2_4_1_y1, decoder_2_4_1_y2,
       decoder_2_4_1_y3;
  wire [3:0] R0_q, R1_q, R2_q, R3_q;

  Decoder_2_4 decoder_2_4_1 (
    .in_1(WriteReg), .Y0(decoder_2_4_1_y0), .Y1(decoder_2_4_1_y1), .Y2(decoder_2_4_1_y2),
    .Y3(decoder_2_4_1_y3));
  and and_1 (and_1_out, decoder_2_4_1_y0, RegWrite);
  and and_2 (and_2_out, decoder_2_4_1_y1, RegWrite);
  and and_3 (and_3_out, decoder_2_4_1_y2, RegWrite);
  and and_4 (and_4_out, decoder_2_4_1_y3, RegWrite);
  Register #(.width(4)) R0 (.D(WriteData), .en(and_1_out), .clk(clock), .Q(R0_q));  // open: clr
  Register #(.width(4)) R1 (.D(WriteData), .en(and_2_out), .clk(clock), .Q(R1_q));  // open: clr
  Register #(.width(4)) R2 (.D(WriteData), .en(and_3_out), .clk(clock), .Q(R2_q));  // open: clr
  Register #(.width(4)) R3 (.D(WriteData), .en(and_4_out), .clk(clock), .Q(R3_q));  // open: clr
  MUX_4_Bit_4X1 mux_4_bit_4x1_1 (
    .I0(R0_q), .I1(R1_q), .S0(ReadReg_A[0]), .S1(ReadReg_A[1]), .I2(R2_q), .I3(R3_q), .Y(ReadData_A));
  MUX_4_Bit_4X1 mux_4_bit_4x1_2 (
    .I0(R0_q), .I1(R1_q), .S0(ReadReg_B[0]), .S1(ReadReg_B[1]), .I2(R2_q), .I3(R3_q), .Y(ReadData_B));
endmodule

module MUX_4X1 (
  input  I0,
  input  I1,
  input  S0,
  input  S1,
  input  I2,
  input  I3,
  output OP
);

  wire mux_2x1_1_p4, mux_2x1_2_p4;

  // MUX_2X1 mux_2x1_1: pin names not known; wires that end beside it: I0, S0, I1, mux_2x1_1_p4
  // MUX_2X1 mux_2x1_2: pin names not known; wires that end beside it: I2, S0, I3, mux_2x1_2_p4
  // MUX_2X1 mux_2x1_3: pin names not known; wires that end beside it: mux_2x1_1_p4, S1, mux_2x1_2_p4, OP
endmodule

module MUX_4_Bit_4X1 (
  input  [3:0] I0,
  input  [3:0] I1,
  input  S0,
  input  S1,
  input  [3:0] I2,
  input  [3:0] I3,
  output [3:0] Y
);

  wire [3:0] mux_4_bit_1_out_4, mux_4_bit_2_out_4;

  MUX_4_Bit mux_4_bit_1 (.A(I0), .B(I1), .S(S0), .out_4(mux_4_bit_1_out_4));
  MUX_4_Bit mux_4_bit_2 (.A(I2), .B(I3), .S(S0), .out_4(mux_4_bit_2_out_4));
  MUX_4_Bit mux_4_bit_3 (.A(mux_4_bit_1_out_4), .B(mux_4_bit_2_out_4), .S(S1), .out_4(Y));
endmodule

module ALU_Supporter (
  input  [3:0] A,
  input  an_d,
  output out_3,
  output out_4,
  output out_5,
  output out_6
);

  and and_1 (out_3, A[0], an_d);
  and and_2 (out_4, A[1], an_d);
  and and_3 (out_5, A[2], an_d);
  and and_4 (out_6, A[3], an_d);
endmodule

module Instruction_Memory (
  input  [7:0] PC,
  input  IR_Enable,
  input  Clock,
  input  Reset,
  output [7:0] INS_REG,
  output [3:0] Operand,
  output [1:0] Reg_B,
  output [1:0] Reg_A,
  output [3:0] OPCODE
);

  ROM rom_1 (.addr(PC), .data(INS_REG));

  assign OPCODE = INS_REG[7:4];
  assign Operand = INS_REG[3:0];
  assign Reg_A = INS_REG[3:2];
  assign Reg_B = INS_REG[1:0];

  // Notes on the sheet:
  //   contents of rom_1 (hex, n*v repeats v):
  //   14 90 84 71 60 75
endmodule

module Program_Counter (
  input  PC_enable,
  input  CLock,
  input  PC_Jump_Taken,
  input  Reset,
  input  [7:0] JUMP_Addr,
  output [7:0] OP
);

  wire not_1_out, or_1_out;
  wire [7:0] alu_supporter_1_out_3, alu_supporter_3_out_3, incrementer_8_bit_1_a, or_2_out;

  or or_1 (or_1_out, PC_Jump_Taken, PC_enable);
  Register register_1 (.D(or_2_out), .en(or_1_out), .clk(CLock), .Q(OP), .clr(Reset));
  // Probe on or_2_out
  Incrementer_8_Bit incrementer_8_bit_1 (.PC(OP), .A(incrementer_8_bit_1_a));
  not not_1 (not_1_out, PC_Jump_Taken);
  ALU_Supporter alu_supporter_1 (
    .A(JUMP_Addr[3:0]), .an_d(PC_Jump_Taken), .out_3(alu_supporter_1_out_3[0]),
    .out_4(alu_supporter_1_out_3[1]), .out_5(alu_supporter_1_out_3[2]), .out_6(alu_supporter_1_out_3[3]));
  ALU_Supporter alu_supporter_2 (
    .A(JUMP_Addr[7:4]), .an_d(PC_Jump_Taken), .out_3(alu_supporter_1_out_3[4]),
    .out_4(alu_supporter_1_out_3[5]), .out_5(alu_supporter_1_out_3[6]), .out_6(alu_supporter_1_out_3[7]));
  ALU_Supporter alu_supporter_3 (
    .A(incrementer_8_bit_1_a[3:0]), .an_d(not_1_out), .out_3(alu_supporter_3_out_3[0]),
    .out_4(alu_supporter_3_out_3[1]), .out_5(alu_supporter_3_out_3[2]), .out_6(alu_supporter_3_out_3[3]));
  ALU_Supporter alu_supporter_4 (
    .A(incrementer_8_bit_1_a[7:4]), .an_d(not_1_out), .out_3(alu_supporter_3_out_3[4]),
    .out_4(alu_supporter_3_out_3[5]), .out_5(alu_supporter_3_out_3[6]), .out_6(alu_supporter_3_out_3[7]));
  assign or_2_out = alu_supporter_3_out_3 | alu_supporter_1_out_3;  // OR_Gate or_2, 8 bits wide
endmodule

module Incrementer_8_Bit (
  input  [7:0] PC,
  output [7:0] A
);

  wire adder_4_bit_2_overflow;
  wire [3:0] bit_extender_1_out, bit_extender_2_out;

  assign bit_extender_1_out = {{3{1'b0}}, 1'b1};  // Bit_Extender bit_extender_1
  Adder_4_Bit adder_4_bit_1 (.A(PC[7:4]), .B(bit_extender_2_out), .OP(A[7:4]));  // open: Overflow
  Adder_4_Bit adder_4_bit_2 (.A(PC[3:0]), .B(bit_extender_1_out), .OP(A[3:0]), .Overflow(adder_4_bit_2_overflow));
  assign bit_extender_2_out = {{3{1'b0}}, adder_4_bit_2_overflow};  // Bit_Extender bit_extender_2
endmodule

module Instruction_Register (
  input  [7:0] Instruction_In,
  input  IR_Load,
  input  Clock,
  output [3:0] Operand,
  output [3:0] Opcode
);

  Register register_1 (.D(Instruction_In), .en(IR_Load), .clk(Clock), .Q({Opcode, Operand}));  // open: clr
endmodule

module Control_Unit (
  input  CLK,
  input  Reset,
  input  [3:0] Opcode,
  output [15:0] ControlWord,
  output [5:0] out_5,
  output [1:0] out_6
);

  wire and_1_out, or_1_out;
  wire [1:0] not_1_out;

  and and_1 (and_1_out, out_5[0], out_5[1]);
  Register #(.width(2)) register_1 (.D(not_1_out), .en(1'b1), .clk(CLK), .Q(out_5[1:0]), .clr(or_1_out));
  or or_1 (or_1_out, Reset, and_1_out);
  // Probe on out_5[1:0]
  not not_1 (not_1_out[0], out_5[0]);
  xor xor_1 (not_1_out[1], out_5[0], out_5[1]);
  ROM #(.addrWidth(6), .dataWidth(16)) Control (.addr({Opcode, out_5[1:0]}), .data(ControlWord));

  assign out_5[5:2] = Opcode;
  assign out_6 = out_5[1:0];

  // Notes on the sheet:
  //   contents of Control (hex, n*v repeats v):
  //   4000 8000 0 0 4000 8000 2a00 0 4000 8000 2040 0 4000 8000 20c0 0 4000 8000 2140 0 4000 8000 2600 0
  //   4000 8000 1008 0 4000 8000 20 0 4000 8000 10 0 4000 8000 21c0 0 4000 8000 0 0 4000 8000 0 0 4000
  //   8000 0 0 4000 8000 0 0 4000 8000 0 0 4000 8000
endmodule

module Adder_2_Bit (
  input  [1:0] A,
  input  [1:0] B,
  output [1:0] out_3
);

  wire adder_1_bit_1_c_out;

  Adder_1_Bit adder_1_bit_1 (.A(A[0]), .B(B[0]), .C_in(1'b0), .Sum(out_3[0]), .C_out(adder_1_bit_1_c_out));
  Adder_1_Bit adder_1_bit_2 (.A(A[1]), .B(B[1]), .C_in(adder_1_bit_1_c_out), .Sum(out_3[1]));  // open: C_out
endmodule

module Data_Memory (
);

  RAM #(.addrWidth(4), .dataWidth(4)) ram_1 ();  // open: addr, we, oe, clk, din, dout
endmodule
